# Fritzing sketch Transistor (saved by Fritzing 0.9.3b)
breadboards: 1

parts:
  Q1 = NPN-Transistor [package="SOT-23 [SMD]"]
  M1 = DC Motor
  Part1 = Arduino Uno (Rev3) - ICSP
  R1 = Resistor [tolerance=±5% resistance=560 package="2010 [SMD]"]

nets:
  GND: Q1.2, Part1.GND
  N1: Q1.0, R1.Pin_1
  N2: Q1.1, M1.pin_2
  12V: M1.pin_1
  N3: Part1.D9_PWM, R1.Pin_0
