# Fritzing sketch PotToServo (saved by Fritzing 0.9.3b)
circuit board: 6.88566cm x 5.36311cm
breadboards: 1

parts:
  J1 = Basic Servo
  R1 = Rotary Potentiometer (Small) [maximum_resistance=100kΩ package=THT]
  Arduino2 = Arduino Uno (Rev3)

nets (from the pcb view):
  GND: J1.gnd, R1.leg2, Arduino2.GND
  VCC: J1.vcc, R1.leg1, Arduino2.5V
  N1: J1.pulse, Arduino2.D9_PWM
  N2: R1.wiper, Arduino2.A2

notes:
  In this example, potentiometer values are read in through an 'Analog In' pin. The values are then used to control the position of a servo motor. Related examples: http://arduino.cc/en/Tutorial/AnalogInput http://arduino.cc/en/Tutorial/Knob

// code stored in the sketch: PotToServo.ino
// Include the Servo library
// https://www.instructables.com/id/Arduino-Servo-Motors/

#include <Servo.h> 
const int analogInPin = A0;

int servoPin = 3; // Declare the Servo pin 

int sensorValue = 0;        // value read from the pot
int outputValue = 0;        // value output to the PWM (analog out)


Servo Servo1; // Create a servo object


void setup() { 
    
   Servo1.attach(servoPin); // We need to attach the servo to the used pin number
     
  Serial.begin(9600); // initialize serial communications at 9600 bps:
}
void loop(){ 

    // read the analog in value:
  sensorValue = analogRead(analogInPin);
  // map it to the range of the analog out:
  outputValue = map(sensorValue, 0, 1023, 0, 255);
    
   Servo1.write(outputValue); // Make servo go to 0 degrees
   Serial.println(sensorValue);
   delay(10); 
   
   
}
